// Logisim project Basic4Bit.circ as structural Verilog: 1 circuit, main circuit main
module main (
  input  in_1,
  input  [7:0] in_2
);

  wire A_pin7, A_pin10, ADD, adder_1_cout, and_1_out, and_2_out, and_3_out, and_4_out, and_6_out, and_7_out,
       and_8_out, and_9_out, and_10_out, and_11_out, B_pin7, B_pin10, C_q, CLK, CMP, instNAND, JPC, JPZ, LDI,
       LDST, n74138_1_pin4, n74138_1_pin5, n74138_1_pin6, nAB, nCLK, nor_1_out, not_3_out, not_4_out,
       not_5_out, not_6_out, not_7_out, not_8_out, not_9_out, not_10_out, not_11_out, nRESET, or_3_out,
       outputA, outputB, outputTEMP, PCH_pin2, PCH_pin7, PCH_pin9, PCH_pin10, PCL_pin7, PCL_pin9, PCL_pin10,
       PT, pull_resistor_2_node, TEMP_pin1, TEMP_pin7, TEMP_pin9, TEMP_pin10, wrA, wrB;
  wire [3:0] adder_1_out, AOUT, BOUT, controlled_buffer_7_out, DATA, nand_1_out, PCH_pin14, PCL_pin14,
       TEMPOUT;
  wire [7:0] ADDRESS, PCH_pin3, rom_1_data;

  Clock clock_1 (.out(CLK));
  // DipSwitch Start: pin names not known
  not not_1 (nRESET, in_1);
  not not_2 (nCLK, CLK);
  _74161 #(.ShowInternalStructure("true")) PCH (
    .pin1(nRESET), .pin2(PCH_pin2), .pin3(PCH_pin3[0]), .pin4(PCH_pin3[1]), .pin5(PCH_pin3[2]),
    .pin6(PCH_pin3[3]), .pin7(PCH_pin7), .pin14(PCH_pin14[0]), .pin13(PCH_pin14[1]), .pin12(PCH_pin14[2]),
    .pin11(PCH_pin14[3]), .pin10(PCH_pin10), .pin9(PCH_pin9));  // open: pin15
  _74161 #(.ShowInternalStructure("true")) PCL (
    .pin1(nRESET), .pin2(nCLK), .pin3(PCH_pin3[4]), .pin4(PCH_pin3[5]), .pin5(PCH_pin3[6]),
    .pin6(PCH_pin3[7]), .pin7(PCL_pin7), .pin15(PCH_pin2), .pin14(PCL_pin14[0]), .pin13(PCL_pin14[1]),
    .pin12(PCL_pin14[2]), .pin11(PCL_pin14[3]), .pin10(PCL_pin10), .pin9(PCL_pin9));
  Hex_Digit_Display #(.decimalPoint("false")) hex_digit_display_1 (.value(AOUT));
  Hex_Digit_Display #(.decimalPoint("false")) hex_digit_display_2 (.value(DATA));
  ROM rom_1 (.addr(ADDRESS), .data(rom_1_data));
  Hex_Digit_Display #(.decimalPoint("false")) hex_digit_display_3 (.value(BOUT));
  Hex_Digit_Display #(.decimalPoint("false")) hex_digit_display_4 (.value({3'b101, in_2[3]}));
  Hex_Digit_Display #(.decimalPoint("false")) hex_digit_display_5 (.value({1'b0, in_2[2:0]}));
  assign ADDRESS = not_3_out ? {PCH_pin14, PCL_pin14} : 8'bz;  // Controlled_Buffer controlled_buffer_1
  not not_3 (not_3_out, not_4_out);
  assign ADDRESS = not_4_out ? {4'b1111, BOUT} : 8'bz;  // Controlled_Buffer controlled_buffer_2
  not not_4 (not_4_out, LDST);
  Hex_Digit_Display #(.decimalPoint("false")) hex_digit_display_6 (.value(ADDRESS[7:4]));
  Hex_Digit_Display #(.decimalPoint("false")) hex_digit_display_7 (.value(ADDRESS[3:0]));
  Hex_Digit_Display #(.decimalPoint("false")) hex_digit_display_8 (.value(TEMPOUT));
  Pull_Resistor pull_resistor_1 (.node(ADDRESS));
  // Probe on rom_1_data
  _74161 #(.ShowInternalStructure("true")) A (
    .pin1(nRESET), .pin2(nCLK), .pin3(DATA[0]), .pin4(DATA[1]), .pin5(DATA[2]), .pin6(DATA[3]),
    .pin7(A_pin7), .pin14(AOUT[0]), .pin13(AOUT[1]), .pin12(AOUT[2]), .pin11(AOUT[3]), .pin10(A_pin10),
    .pin9(wrA));  // open: pin15
  _74161 #(.ShowInternalStructure("true")) B (
    .pin1(nRESET), .pin2(nCLK), .pin3(DATA[0]), .pin4(DATA[1]), .pin5(DATA[2]), .pin6(DATA[3]),
    .pin7(B_pin7), .pin14(BOUT[0]), .pin13(BOUT[1]), .pin12(BOUT[2]), .pin11(BOUT[3]), .pin10(B_pin10),
    .pin9(wrB));  // open: pin15
  D_Flip_Flop C (.D(adder_1_cout), .clk(ADD), .Q(C_q));  // open: Qn, preset, reset
  assign DATA = nor_1_out ? in_2[7:4] : 4'bz;  // Controlled_Buffer controlled_buffer_3
  nor nor_1 (nor_1_out, outputTEMP, outputB, outputA);
  assign DATA = outputA ? AOUT : 4'bz;  // Controlled_Buffer controlled_buffer_4
  assign DATA = outputB ? BOUT : 4'bz;  // Controlled_Buffer controlled_buffer_5
  assign DATA = outputTEMP ? TEMPOUT : 4'bz;  // Controlled_Buffer controlled_buffer_6
  Adder #(.width(4)) adder_1 (.a(DATA), .b(AOUT), .out(adder_1_out), .cin(C_q), .cout(adder_1_cout));
  assign controlled_buffer_7_out = instNAND ? adder_1_out : 4'bz;  // Controlled_Buffer controlled_buffer_7
  not not_5 (not_5_out, instNAND);
  assign nand_1_out = ~(AOUT & DATA);  // NAND_Gate nand_1, 4 bits wide
  assign controlled_buffer_7_out = not_5_out ? nand_1_out : 4'bz;  // Controlled_Buffer controlled_buffer_8
  and and_1 (and_1_out, LDI, PT);
  not not_6 (not_6_out, in_2[1]);
  not not_7 (not_7_out, in_2[0]);
  _74161 #(.ShowInternalStructure("true")) TEMP (
    .pin1(TEMP_pin1), .pin2(CLK), .pin3(controlled_buffer_7_out[0]), .pin4(controlled_buffer_7_out[1]),
    .pin5(controlled_buffer_7_out[2]), .pin6(controlled_buffer_7_out[3]), .pin7(TEMP_pin7),
    .pin14(TEMPOUT[0]), .pin13(TEMPOUT[1]), .pin12(TEMPOUT[2]), .pin11(TEMPOUT[3]), .pin10(TEMP_pin10),
    .pin9(TEMP_pin9));  // open: pin15
  or or_1 (wrB, and_1_out, nAB);
  and and_2 (and_2_out, in_2[2], in_2[0]);
  and and_3 (and_3_out, in_2[2], in_2[1]);
  and and_4 (and_4_out, not_7_out, not_6_out, in_2[3]);
  and and_5 (TEMP_pin9, ADD, instNAND);
  _74138 #(.ShowInternalStructure("true")) u_74138_1 (
    .pin1(in_2[0]), .pin2(in_2[1]), .pin3(in_2[2]), .pin4(n74138_1_pin4), .pin5(n74138_1_pin5),
    .pin6(n74138_1_pin6), .pin7(JPC), .pin15(LDI), .pin14(PT), .pin13(ADD), .pin12(instNAND), .pin11(LDST),
    .pin10(CMP), .pin9(JPZ));
  _7414 #(.ShowInternalStructure("true")) u_7414_1 (
    .pin13(in_2[3]), .pin12(nAB));  // open: pin1, pin2, pin3, pin4, pin5, pin6, pin11, pin10, pin9, pin8
  or or_2 (wrA, and_2_out, and_3_out, and_4_out);
  _7400 #(.ShowInternalStructure("true")) u_7400_1 ();  // open: pin1, pin2, pin3, pin4, pin5, pin6, pin13, pin12, pin11, pin10, pin9, pin8
  not not_8 (not_8_out, ADD);
  or or_3 (or_3_out, not_8_out, not_9_out);
  not not_9 (not_9_out, instNAND);
  and and_6 (and_6_out, in_2[3], or_3_out);
  not not_10 (not_10_out, PT);
  not not_11 (not_11_out, PT);
  and and_7 (and_7_out, not_11_out, nAB, CLK);
  and and_8 (and_8_out, nCLK, and_6_out);
  and and_9 (and_9_out, and_6_out, CLK);
  and and_10 (and_10_out, CLK, PT, nAB);
  and and_11 (and_11_out, not_10_out, in_2[3], CLK);
  or or_4 (outputA, and_11_out, pull_resistor_2_node);
  Pull_Resistor pull_resistor_2 (.node(pull_resistor_2_node));
  or or_5 (outputB, and_7_out, and_8_out);
  or or_6 (outputTEMP, and_9_out, and_10_out);
  // also tied to GND on the sheet: {A_pin7, A_pin10, B_pin7, B_pin10, TEMP_pin7, n74138_1_pin4, n74138_1_pin5, TEMP_pin10}
  // also tied to VCC on the sheet: {PCH_pin7, PCL_pin7, PCH_pin10, PCH_pin9, PCL_pin10, PCL_pin9, TEMP_pin1, n74138_1_pin6}

  // Other names for the same wires on the sheet: DATAEXT[7:0] = in_2; INST[2:0] = in_2[2:0]; AB = in_2[3];
  //   RESET = in_1

  // Notes on the sheet:
  //   contents of rom_1 (hex, n*v repeats v):
  //   50 9 68 a
  //   Registers
endmodule
